// Logisim project A2_GROUP-2.circ as structural Verilog: 3 circuits, main circuit main
module main (
  input  CS2,
  input  CS1,
  input  CS0,
  input  A0,
  input  B0,
  input  A1,
  input  B1,
  input  A2,
  input  B2,
  input  A3,
  input  B3,
  output Cout,
  output S3,
  output S2,
  output S1,
  output S0,
  output Z,
  output S,
  output C,
  output V
);

  wire _7432_2_2_out, _7432_2_3_out, _7432_2_out, modifiedadder_1_cprev, xi_yi_ckt_1_cin, xi_yi_ckt_1_x0,
       xi_yi_ckt_1_x1, xi_yi_ckt_1_x2, xi_yi_ckt_1_x3, xi_yi_ckt_1_y0, xi_yi_ckt_1_y1, xi_yi_ckt_1_y2,
       xi_yi_ckt_1_y3;

  Xi_Yi_Ckt xi_yi_ckt_1 (
    .S2(CS2), .S1(CS1), .S0(CS0), .A0(A0), .B0(B0), .A1(A1), .B1(B1), .A2(A2), .B2(B2), .A3(A3), .B3(B3),
    .Cin(xi_yi_ckt_1_cin), .X3(xi_yi_ckt_1_x3), .X2(xi_yi_ckt_1_x2), .X1(xi_yi_ckt_1_x1),
    .X0(xi_yi_ckt_1_x0), .Y3(xi_yi_ckt_1_y3), .Y2(xi_yi_ckt_1_y2), .Y1(xi_yi_ckt_1_y1), .Y0(xi_yi_ckt_1_y0));
  modifiedAdder modifiedadder_1 (
    .X3(xi_yi_ckt_1_x3), .Cin(xi_yi_ckt_1_cin), .Y3(xi_yi_ckt_1_y3), .X2(xi_yi_ckt_1_x2),
    .Y2(xi_yi_ckt_1_y2), .X1(xi_yi_ckt_1_x1), .Y1(xi_yi_ckt_1_y1), .X0(xi_yi_ckt_1_x0), .Y0(xi_yi_ckt_1_y0),
    .S3(S), .S2(S2), .S1(S1), .S0(S0), .Cprev(modifiedadder_1_cprev), .Cout(C));
  xor _7486_2 (Z, _7432_2_3_out, 1'b1);
  or _7432_2 (_7432_2_out, S, S2);
  or _7432_2_2 (_7432_2_2_out, S1, S0);
  or _7432_2_3 (_7432_2_3_out, _7432_2_out, _7432_2_2_out);
  xor _7486_2_2 (V, modifiedadder_1_cprev, C);

  assign Cout = C;
  assign S3 = S;

  // Notes on the sheet:
  //   12
  //   13
  //   11
  //   5
  //   4
  //   6
  //   13
  //   10
  //   8
  //   12
  //   11
  //   9
  //   1
  //   3
  //   2
endmodule

// Xi-Yi Ckt
module Xi_Yi_Ckt (
  input  S2,
  input  S1,
  input  S0,
  input  A0,
  input  B0,
  input  A1,
  input  B1,
  input  A2,
  input  B2,
  input  A3,
  input  B3,
  output Cin,
  output X3,
  output X2,
  output X1,
  output X0,
  output Y3,
  output Y2,
  output Y1,
  output Y0
);

  wire _7404_2_out, _7404_3_out, _7404_4_out, _7404_5_out, _7404_6_out, _7404_out, _7408_1_2_out,
       _7408_1_3_out, _7408_1_out, _7408_2_2_out, _7408_2_out, _7432_1_2_out, _7432_1_3_out, _7432_1_4_out,
       _7432_1_out, _7432_2_out, _7486_1_2_out, _7486_1_3_out, _7486_1_4_out, _7486_1_out, _7486_2_out;

  not _7404 (_7404_out, S0);
  not _7404_2 (_7404_2_out, S2);
  and _7408_2 (_7408_2_out, _7404_2_out, _7404_out);
  and _7408_1 (_7408_1_out, S2, S1);
  not _7404_3 (_7404_3_out, S1);
  and _7408_2_2 (_7408_2_2_out, S2, S0);
  or _7432_2 (_7432_2_out, S1, _7408_2_2_out);
  and _7408_1_2 (_7408_1_2_out, S2, _7404_3_out);
  not _7404_4 (_7404_4_out, B3);
  not _7404_5 (_7404_5_out, B2);
  not _7404_6 (_7404_6_out, B1);
  xor _7486_2 (_7486_2_out, B0, 1'b1);
  and _7408_1_3 (_7408_1_3_out, _7408_1_2_out, S0);
  xor _7486_1 (_7486_1_out, _7408_1_out, A0);
  or _7432_1 (_7432_1_out, A0, B0);
  xor _7486_1_2 (_7486_1_2_out, _7408_1_out, A1);
  or _7432_1_2 (_7432_1_2_out, A1, B1);
  xor _7486_1_3 (_7486_1_3_out, _7408_1_out, A2);
  or _7432_1_3 (_7432_1_3_out, A2, B2);
  xor _7486_1_4 (_7486_1_4_out, _7408_1_out, A3);
  or _7432_1_4 (_7432_1_4_out, A3, B3);
  // DIP_74157 dip_74157_1: pin names not known; wires that end beside it: _7408_1_3_out, _7486_1_out, _7432_1_out, X0, _7486_1_2_out, _7432_1_2_out, X1, 1'b0, _7486_1_4_out, _7432_1_4_out, X3, _7486_1_3_out, _7432_1_3_out, X2
  // DIP_74157 dip_74157_2: pin names not known; wires that end beside it: _7408_2_out, _7486_2_out, 1'b1, Y0, _7404_6_out, 1'b1, Y1, _7432_2_out, _7404_4_out, 1'b1, Y3, _7404_5_out, 1'b1, Y2
  and _7408_2_3 (Cin, _7404_out, _7408_1_2_out);

  // Notes on the sheet:
  //   3
  //   5
  //   1
  //   2
  //   1
  //   1
  //   2
  //   S0'
  //   4
  //   6
  //   9
  //   10
  //   8
  //   s2's0'
  //   3
  //   S2S1
  //   2
  //   3
  //   1
  //   2
  //   4
  //   5
  //   3
  //   s2s1'
  //   6
  //   s1+s0s2
  //   13
  //   10
  //   9
  //   10
  //   9
  //   13
  //   12
  //   13\
  //   12
  //   10
  //   9
  //   10
  //   9
  //   4
  //   5
  //   4
  //   5
  //   1
  //   2
  //   1
  //   2
  //   B3'
  //   8
  //   9
  //   B2'
  //   11
  //   10
  //   B1'
  //   12
  //   B0'
  //   8
  //   s2s1's0
  //   8
  //   11
  //   11
  //   8
  //   8
  //   6
  //   6
  //   3
  //   3
  //   4
  //   5
  //   6
endmodule

// Adder
module modifiedAdder (
  input  X3,
  input  Cin,
  input  Y3,
  input  X2,
  input  Y2,
  input  X1,
  input  Y1,
  input  X0,
  input  Y0,
  output S3,
  output S2,
  output S1,
  output S0,
  output Cprev,
  output Cout
);

  // adderseparate_main main_1: pin names not known; wires that end beside it: 1'b0, S2, X2, Y2, 1'b1, S1, Y1, X1, 1'b0, Cprev, Cin, 1'b0, Y0, X0, S0
  // adderseparate_main main_2: pin names not known; wires that end beside it: 1'b0, 1'b0, 1'b0, 1'b1, Cout, 1'b0, 1'b0, 1'b0, Cprev, 1'b0, Y3, X3, S3

  // Notes on the sheet:
  //   1
  //   2
endmodule
