// Logisim project normalizer.circ as structural Verilog: 6 circuits, main circuit normalizer
// NMR
module normalizer (
  input  [10:0] exponent_input,
  input  [31:0] significand_input,
  output [10:0] normalized_Exponent,
  output [31:0] normalized_Significand,
  output underflow,
  output overflow
);

  wire adder_substractorlib_1_overflow, adder_substractorlib_1_underflow, and_1_out, multiplexer_4_out,
       multiplexer_5_out, one_checker_1_isone, priority_encoder_1_en_out, xor_1_out, zero_checker_1_iszero;
  wire [4:0] multiplexer_1_out, priority_encoder_1_out, subtractor_1_out;
  wire [10:0] adder_substractorlib_1_output_exponent;
  wire [31:0] shifter_1_output;

  xor xor_1 (xor_1_out, significand_input[31], 1'b1);
  and and_1 (and_1_out, xor_1_out, priority_encoder_1_en_out);
  Priority_Encoder #(.select(5)) priority_encoder_1 (
    .in0(significand_input[0]), .in1(significand_input[1]), .in2(significand_input[2]),
    .in3(significand_input[3]), .in4(significand_input[4]), .in5(significand_input[5]),
    .in6(significand_input[6]), .in7(significand_input[7]), .in8(significand_input[8]),
    .in9(significand_input[9]), .in10(significand_input[10]), .in11(significand_input[11]),
    .in12(significand_input[12]), .in13(significand_input[13]), .in14(significand_input[14]),
    .in15(significand_input[15]), .in16(significand_input[16]), .in17(significand_input[17]),
    .in18(significand_input[18]), .in19(significand_input[19]), .in20(significand_input[20]),
    .in21(significand_input[21]), .in22(significand_input[22]), .in23(significand_input[23]),
    .in24(significand_input[24]), .in25(significand_input[25]), .in26(significand_input[26]),
    .in27(significand_input[27]), .in28(significand_input[28]), .in29(significand_input[29]),
    .in30(significand_input[30]), .in31(1'b0), .out(priority_encoder_1_out),
    .en_out(priority_encoder_1_en_out), .en_in(1'b1));  // open: gs
  Shifter shifter_1 (
    .\input (significand_input), .shiftAmmount(multiplexer_1_out), .left_right(significand_input[31]),
    .\output (shifter_1_output));
  Subtractor #(.width(5)) subtractor_1 (
    .a(5'b11110), .b(priority_encoder_1_out), .out(subtractor_1_out));  // open: bin, bout
  Multiplexer #(.width(5), .disabled(0), .enable("false")) multiplexer_1 (
    .in0(subtractor_1_out), .in1(5'b00001), .out(multiplexer_1_out), .sel(significand_input[31]));
  Multiplexer #(.width(11), .disabled(0), .enable("false")) multiplexer_2 (
    .in0(adder_substractorlib_1_output_exponent), .in1({11{1'b0}}), .out(normalized_Exponent), .sel(and_1_out));
  Multiplexer #(.width(32), .disabled(0), .enable("false")) multiplexer_3 (
    .in0(shifter_1_output), .in1({32{1'b0}}), .out(normalized_Significand), .sel(and_1_out));
  adder_substractorLib adder_substractorlib_1 (
    .input_exponent(exponent_input), .add_sub_amount(multiplexer_1_out),
    .underflow(adder_substractorlib_1_underflow), .overflow(adder_substractorlib_1_overflow),
    .add_sub(significand_input[31]), .output_exponent(adder_substractorlib_1_output_exponent));
  Multiplexer #(.disabled(0), .enable("false")) multiplexer_4 (
    .in0(adder_substractorlib_1_underflow), .in1(1'b0), .out(multiplexer_4_out), .sel(and_1_out));
  Multiplexer #(.disabled(0), .enable("false")) multiplexer_5 (
    .in0(adder_substractorlib_1_overflow), .in1(1'b0), .out(multiplexer_5_out), .sel(and_1_out));
  zero_checker zero_checker_1 (.exponent(normalized_Exponent), .isZero(zero_checker_1_iszero));
  or or_1 (underflow, zero_checker_1_iszero, multiplexer_4_out);
  one_checker one_checker_1 (.exponent(normalized_Exponent), .isOne(one_checker_1_isone));
  or or_2 (overflow, one_checker_1_isone, multiplexer_5_out);

  // Notes on the sheet:
  //   encoded value
  //   highest encoded value
  //   substractor
  //   right shift ammount
endmodule

// shifter
module Shifter (
  input  [31:0] \input ,
  input  [4:0] shiftAmmount,
  input  left_right,
  output [31:0] \output 
);

  wire [31:0] arbitary_rightshifter_1_p3, arbitrary_leftshifter_1_p3;

  // arbitrary_leftShifter arbitrary_leftshifter_1: pin names not known; wires that end beside it: \input , shiftAmmount, arbitrary_leftshifter_1_p3
  // arbitary_rightShifter arbitary_rightshifter_1: pin names not known; wires that end beside it: \input , shiftAmmount, arbitary_rightshifter_1_p3
  Multiplexer #(.width(32), .disabled(0), .enable("false")) multiplexer_1 (
    .in0(arbitrary_leftshifter_1_p3), .in1(arbitary_rightshifter_1_p3), .out(\output ), .sel(left_right));
endmodule

// A/S
module adder_substractorLib (
  input  [10:0] input_exponent,
  input  [4:0] add_sub_amount,
  input  add_sub,
  output underflow,
  output [10:0] output_exponent,
  output overflow
);

  wire adder_1_cout, not_1_out, subtractor_1_bout;
  wire [10:0] adder_1_out, subtractor_1_out;

  Subtractor #(.width(11)) subtractor_1 (
    .a(input_exponent), .b({{6{1'b0}}, add_sub_amount}), .out(subtractor_1_out), .bin(1'b0),
    .bout(subtractor_1_bout));
  Adder #(.width(11)) adder_1 (
    .a(input_exponent), .b({{6{1'b0}}, add_sub_amount}), .out(adder_1_out), .cin(1'b0), .cout(adder_1_cout));
  and and_1 (overflow, adder_1_cout, add_sub);
  not not_1 (not_1_out, add_sub);
  and and_2 (underflow, not_1_out, subtractor_1_bout);
  Multiplexer #(.width(11), .disabled(0), .enable("false")) multiplexer_1 (
    .in0(subtractor_1_out), .in1(adder_1_out), .out(output_exponent), .sel(add_sub));
endmodule

// RNMR
module rounded_normalizer (
  input  [10:0] exponent_input,
  input  [31:0] significand_input,
  output [10:0] normalized_Exponent,
  output overflow,
  output [31:0] normalized_Significand
);

  wire adder_1_cout, one_checker_1_isone;
  wire [31:0] n1_bit_rightshifter_1_p3;

  Adder #(.width(11)) adder_1 (
    .a(exponent_input), .b({11{1'b0}}), .out(normalized_Exponent), .cin(significand_input[31]),
    .cout(adder_1_cout));
  // _1_bit_rightShifter 1_bit_rightshifter_1: pin names not known; wires that end beside it: significand_input, 1'b1, n1_bit_rightshifter_1_p3
  Multiplexer #(.width(32), .disabled(0), .enable("false")) multiplexer_1 (
    .in0(significand_input), .in1(n1_bit_rightshifter_1_p3), .out(normalized_Significand),
    .sel(significand_input[31]));
  one_checker one_checker_1 (.exponent(normalized_Exponent), .isOne(one_checker_1_isone));
  or or_1 (overflow, one_checker_1_isone, adder_1_cout);
endmodule

// z
module zero_checker (
  input  [10:0] exponent,
  output isZero
);

  wire or_1_out, or_2_out;

  or or_1 (or_1_out, exponent[0], exponent[1], exponent[2], exponent[3], exponent[4]);
  or or_2 (or_2_out, exponent[5], exponent[6], exponent[7], exponent[8], exponent[9], exponent[10]);
  nor nor_1 (isZero, or_1_out, or_2_out);
endmodule

// OC
module one_checker (
  input  [10:0] exponent,
  output isOne
);

  wire and_1_out, and_2_out;

  and and_1 (and_1_out, exponent[0], exponent[1], exponent[2], exponent[3], exponent[4]);
  and and_2 (and_2_out, exponent[5], exponent[6], exponent[7], exponent[8], exponent[9], exponent[10]);
  and and_3 (isOne, and_1_out, and_2_out);
endmodule
